# Fritzing sketch car_wiring (saved by Fritzing 1.0.4)
perfboards: 1

parts:
  U1 = ESP32-38PinWide [part_number=ESP32-38PinWide]
  HC-SR04_Sensor_1 = HC-SR04 Ultrasonic Distance Sensor
  HC-SR04_Sensor_2 = HC-SR04 Ultrasonic Distance Sensor
  LED1 = smd LED [color="Blue (470nm)" package="0805 [SMD]"]
  M1 = INA3221 Triple Channel Current/Voltage Monitor Module [part_number=CJMCU-3221]  # not connected
  L298N2 = L298N DC motor driver
  M2 = DC Motor [voltage_(max)=6V voltage_(min)=3V]
  TB1 = KF301-2 [part_number=KF301-2 package="screwterminal-5mm 2 position"]
  J1 = Basic Servo
  VCC1 = Battery [internal_resistance=0.1Ω]

nets:
  N1: U1.GPIO25, L298N2.IN2
  N2: U1.GPIO26, L298N2.IN1
  N3: U1.GPIO27, L298N2.ENA
  N4: U1.GPIO12, LED1.anode
  GND: U1.GND, HC-SR04_Sensor_2.GND, LED1.cathode, L298N2.GND, TB1.1
  N5: U1.GPIO13, J1.pulse
  VIN: U1.VIN, J1.vcc
  N6: U1.GPIO16, HC-SR04_Sensor_2.ECHO
  N7: U1.GPIO17, HC-SR04_Sensor_2.TRIG
  N8: U1.GPIO18, HC-SR04_Sensor_1.TRIG
  N9: U1.GPIO19, HC-SR04_Sensor_1.ECHO
  N10: HC-SR04_Sensor_1.GND, VCC1.-
  N11: L298N2.OUT1, M2.pin_2
  N12: L298N2.OUT2, M2.pin_1
  N13: L298N2.12V, TB1.2, VCC1.+

custom parts:
  ESP32-38PinWide: Generic 38-Pin ESP32 with wide format (only access to one side of pins on a breadboard) based on Stephen Lilley's HiLetgo ESP-WROOM-32 ESP32 ESP-32S Development Board.
  INA3221 Triple Channel Current/Voltage Monitor Module: INA3221 Triple Channel Current/Voltage Monitor Module Links: INA3221 product information
  L298N DC motor driver: 2x DC motor driver with 78M05 positive voltage regulator (7..35 V) L298N: max 46 V, 2 A Set 5 V Enable jumper to enable 5 V regultor (needed for the L298N) and +5 V output at screw terminal or supply external +5 V at screw terminal Set ENA and/or ENB to +5 V to enable motor permanently or supply ENA and/or ENB with PWM signal IN1 and IN2 set rotation directory for motor A (OUT1/OUT2) IN2 and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
  KF301-2: KF301-3 is a 3 position screw terminal header block with male through hole PCB pins on 5mm spacing
